// Logisim project LIFT_ahan.circ as structural Verilog: 3 circuits, main circuit main
module main (
  input  [3:0] Lift_A,
  input  [3:0] Lift_B,
  input  in_3,
  input  in_4,
  output [3:0] out_5,
  output [3:0] out_6
);

  wire and_1_out, and_2_out, and_3_out, and_4_out, and_5_out, button_1_out, button_2_out, button_3_out,
       button_4_out, button_5_out, button_6_out, button_7_out, button_8_out, button_9_out, button_10_out,
       button_11_out, button_12_out, button_13_out, button_14_out, button_15_out, button_16_out,
       comparator_1_gt, comparator_2_gt, comparator_3_eq, comparator_3_gt, comparator_3_lt, not_1_out,
       not_2_out, not_3_out, not_4_out, or_1_out, or_2_out;
  wire [3:0] priority_encoder_1_out, subtractor_1_out, subtractor_2_out, subtractor_3_out, subtractor_4_out;

  Button button_1 (.out(button_1_out));
  Button button_2 (.out(button_2_out));
  Button button_3 (.out(button_3_out));
  Button button_4 (.out(button_4_out));
  Button button_5 (.out(button_5_out));
  Button button_6 (.out(button_6_out));
  Button button_7 (.out(button_7_out));
  Button button_8 (.out(button_8_out));
  Button button_9 (.out(button_9_out));
  Button button_10 (.out(button_10_out));
  Button button_11 (.out(button_11_out));
  Button button_12 (.out(button_12_out));
  Button button_13 (.out(button_13_out));
  Button button_14 (.out(button_14_out));
  Button button_15 (.out(button_15_out));
  Button button_16 (.out(button_16_out));
  Priority_Encoder #(.select(4)) priority_encoder_1 (
    .in0(button_1_out), .in1(button_2_out), .in2(button_3_out), .in3(button_4_out), .in4(button_5_out),
    .in5(button_6_out), .in6(button_7_out), .in7(button_8_out), .in8(button_9_out), .in9(button_10_out),
    .in10(button_11_out), .in11(button_12_out), .in12(button_13_out), .in13(button_14_out),
    .in14(button_15_out), .in15(button_16_out), .out(priority_encoder_1_out));  // open: gs, en_out, en_in
  Hex_Digit_Display hex_digit_display_1 (.value(priority_encoder_1_out));  // open: dp
  Hex_Digit_Display hex_digit_display_2 (.value(Lift_B));  // open: dp
  Hex_Digit_Display hex_digit_display_3 (.value(Lift_A));  // open: dp
  Subtractor #(.width(4)) subtractor_1 (
    .a(Lift_A), .b(priority_encoder_1_out), .out(subtractor_1_out));  // open: bin, bout
  Subtractor #(.width(4)) subtractor_2 (
    .a(priority_encoder_1_out), .b(Lift_A), .out(subtractor_2_out));  // open: bin, bout
  Subtractor #(.width(4)) subtractor_3 (
    .a(Lift_B), .b(priority_encoder_1_out), .out(subtractor_3_out));  // open: bin, bout
  Subtractor #(.width(4)) subtractor_4 (
    .a(priority_encoder_1_out), .b(Lift_B), .out(subtractor_4_out));  // open: bin, bout
  LED led_1 (.in(and_4_out));
  LED led_2 (.in(or_1_out));
  LED led_3 (.in(or_2_out));
  Comparator #(.mode("unsigned"), .width(4)) comparator_1 (
    .a(subtractor_1_out), .b(subtractor_2_out), .gt(comparator_1_gt));  // open: eq, lt
  Comparator #(.mode("unsigned"), .width(4)) comparator_2 (
    .a(subtractor_3_out), .b(subtractor_4_out), .gt(comparator_2_gt));  // open: eq, lt
  Multiplexer #(.width(4)) multiplexer_1 (
    .in0(subtractor_1_out), .in1(subtractor_2_out), .out(out_5), .sel(comparator_1_gt));
  Multiplexer #(.width(4)) multiplexer_2 (
    .in0(subtractor_3_out), .in1(subtractor_4_out), .out(out_6), .sel(comparator_2_gt));
  Comparator #(.mode("unsigned"), .width(4)) comparator_3 (
    .a(out_5), .b(out_6), .gt(comparator_3_gt), .eq(comparator_3_eq), .lt(comparator_3_lt));
  not not_1 (not_1_out, in_3);
  not not_2 (not_2_out, in_4);
  not not_3 (not_3_out, or_1_out);
  not not_4 (not_4_out, or_2_out);
  and and_1 (and_1_out, comparator_3_eq, not_1_out);
  or or_1 (or_1_out, and_1_out, and_2_out);
  and and_2 (and_2_out, comparator_3_lt, not_1_out);
  and and_3 (and_3_out, comparator_3_gt, not_2_out);
  and and_4 (and_4_out, not_3_out, not_4_out);
  LED led_4 (.in(and_4_out));
  LED led_5 (.in(or_1_out));
  LED led_6 (.in(or_2_out));
  or or_2 (or_2_out, and_5_out, and_3_out);
  and and_5 (and_5_out, not_2_out, comparator_3_eq);

  // Notes on the sheet:
  //   0
  //   1
  //   2
  //   3
  //   4
  //   5
  //   6
  //   7
  //   8
  //   9
  //   10
  //   11
  //   12
  //   13
  //   14
  //   15
  //   LIFT 1 OVERCROWDED
  //   LIFT 2 OVERCROWDED
  //   Please Wait
  //   Lift A
  //   Lift B
  //   Please Wait
  //   Lift A
  //   Lift B
endmodule

module b2d (
  input  kat0,
  input  kat1,
  input  kat2,
  output a,
  output b,
  output c,
  output d,
  output e,
  output f,
  output g,
  output nokta
);

  wire and_1_out, and_2_out, and_3_out, and_4_out, and_5_out, and_6_out, and_7_out, and_8_out, and_9_out,
       and_10_out, and_11_out, not_1_out, not_2_out, not_3_out, not_4_out, not_5_out, not_6_out, not_7_out,
       not_8_out, not_9_out, not_10_out, not_11_out, not_12_out, not_13_out, not_14_out, not_15_out,
       not_16_out, not_17_out, not_18_out, not_19_out, not_20_out, not_21_out, not_22_out, not_23_out,
       not_24_out, not_25_out, not_26_out;

  not not_1 (not_1_out, kat0);
  not not_2 (not_2_out, kat1);
  not not_3 (not_3_out, kat1);
  not not_4 (not_4_out, kat2);
  not not_5 (not_5_out, kat0);
  not not_6 (not_6_out, kat1);
  not not_7 (not_7_out, kat0);
  not not_8 (not_8_out, kat2);
  not not_9 (not_9_out, kat1);
  not not_10 (not_10_out, kat2);
  not not_11 (not_11_out, kat0);
  not not_12 (not_12_out, kat2);
  not not_13 (not_13_out, kat1);
  not not_14 (not_14_out, kat2);
  not not_15 (not_15_out, kat0);
  not not_16 (not_16_out, kat1);
  not not_17 (not_17_out, kat1);
  not not_18 (not_18_out, kat2);
  not not_19 (not_19_out, kat0);
  not not_20 (not_20_out, kat1);
  not not_21 (not_21_out, kat1);
  not not_22 (not_22_out, kat2);
  not not_23 (not_23_out, kat1);
  not not_24 (not_24_out, kat2);
  not not_25 (not_25_out, kat0);
  not not_26 (not_26_out, kat1);
  and and_1 (and_1_out, not_1_out, not_2_out, kat2);
  and and_2 (and_2_out, kat0, not_3_out, not_4_out);
  and and_3 (and_3_out, not_5_out, not_6_out, kat2);
  and and_4 (and_4_out, not_7_out, kat1, not_8_out);
  and and_5 (and_5_out, kat0, not_9_out, not_10_out);
  and and_6 (and_6_out, not_11_out, kat1, not_12_out);
  and and_7 (and_7_out, kat0, not_13_out, not_14_out);
  and and_8 (and_8_out, not_15_out, not_16_out, kat2);
  and and_9 (and_9_out, kat0, not_17_out, not_18_out);
  and and_10 (and_10_out, not_19_out, not_20_out, kat2);
  and and_11 (and_11_out, kat0, not_21_out, not_22_out);
  and and_12 (f, kat0, not_23_out, not_24_out);
  and and_13 (g, not_25_out, not_26_out, kat2);
  or or_1 (a, and_1_out, and_2_out);
  or or_2 (b, and_3_out, and_4_out, and_5_out);
  or or_3 (c, and_6_out, and_7_out);
  or or_4 (d, and_8_out, and_9_out);
  or or_5 (e, and_10_out, and_11_out);
  _7_Segment_Display u_7_segment_display_1 ();  // open: g, f, a, b, e, d, c, dp

  assign nokta = 1'b1;
endmodule

module BUTTONS (
  input  [3:0] in_1,
  input  [3:0] in_2,
  input  [3:0] in_3,
  input  [3:0] in_4,
  input  [3:0] in_5,
  input  [3:0] in_6,
  input  [3:0] in_7,
  input  [3:0] in_8,
  input  [3:0] in_9,
  input  [3:0] in_10,
  input  [3:0] in_11,
  input  [3:0] in_12,
  input  [3:0] in_13,
  input  [3:0] in_14,
  input  [3:0] in_15,
  input  [3:0] in_16,
  input  [3:0] in_17,
  output [3:0] out_18
);

  Multiplexer #(.select(4), .width(4)) multiplexer_1 (
    .in0(in_17), .in1(in_16), .in2(in_15), .in3(in_14), .in4(in_12), .in5(in_11), .in6(in_10), .in7(in_9),
    .in8(in_8), .in9(in_7), .in10(in_6), .in11(in_5), .in12(in_4), .in13(in_3), .in14(in_2), .in15(in_1),
    .out(out_18), .sel(in_13));
endmodule
