// Logisim project UP_DOWN_FIXED.circ as structural Verilog: 1 circuit, main circuit main
module main (
  input  entry,
  input  exit,
  input  in_3,
  input  [3:0] in_4,
  input  [3:0] in_5
);

  wire and_1_out, and_2_out, and_3_out, and_4_out, and_5_out, and_6_out, and_7_out, button_1_out,
       comparator_1_eq, comparator_2_eq, not_1_out, not_2_out, or_1_out, or_2_out, or_3_out, t_ff_1_qn,
       t_ff_2_qn;
  wire [2:0] t_ff_1_q;

  Button button_1 (.out(button_1_out));
  or or_1 (or_1_out, and_2_out, and_5_out);
  and and_1 (and_1_out, button_1_out, or_1_out);
  and and_2 (and_2_out, not_2_out, entry);
  T_Flip_Flop t_ff_1 (.clk(and_1_out), .T(1'b1), .Q(t_ff_1_q[0]), .Qn(t_ff_1_qn));  // open: preset, reset, en
  Comparator #(.width(4), .mode("unsigned")) comparator_1 (
    .a({in_3, t_ff_1_q}), .b(in_5), .eq(comparator_1_eq));  // open: gt, lt
  and and_3 (and_3_out, entry, t_ff_1_q[0]);
  or or_2 (or_2_out, and_3_out, and_4_out);
  and and_4 (and_4_out, t_ff_1_qn, exit);
  LED led_1 (.in(comparator_1_eq));
  T_Flip_Flop t_ff_2 (.clk(and_1_out), .T(or_2_out), .Q(t_ff_1_q[1]), .Qn(t_ff_2_qn));  // open: preset, reset, en
  not not_1 (not_1_out, comparator_1_eq);
  and and_5 (and_5_out, exit, not_1_out);
  and and_6 (and_6_out, and_3_out, t_ff_1_q[1]);
  or or_3 (or_3_out, and_6_out, and_7_out);
  and and_7 (and_7_out, and_4_out, t_ff_2_qn);
  T_Flip_Flop t_ff_3 (.clk(and_1_out), .T(or_3_out), .Q(t_ff_1_q[2]));  // open: Qn, preset, reset, en
  Comparator #(.width(4), .mode("unsigned")) comparator_2 (
    .a({in_3, t_ff_1_q}), .b(in_4), .eq(comparator_2_eq));  // open: gt, lt
  LED led_2 (.in(comparator_2_eq));
  Hex_Digit_Display hex_digit_display_1 (.value({in_3, t_ff_1_q}));  // open: dp
  not not_2 (not_2_out, comparator_2_eq);

  // Notes on the sheet:
  //   Empty
  //   Full
endmodule
