// Logisim project lockkey (1).circ as structural Verilog: 1 circuit, main circuit main
module main (
  input  in_1
);

  wire and_1_out, and_2_out, and_3_out, and_4_out, button_1_out, button_2_out, button_3_out, comparator_1_eq,
       comparator_2_eq, comparator_3_eq, comparator_4_eq, not_1_out, not_2_out, or_1_out, or_2_out;
  wire [2:0] counter_2_q;
  wire [3:0] counter_1_q, d_ff_1_q;

  Button button_1 (.out(button_1_out));
  Button button_2 (.out(button_2_out));
  and and_1 (and_1_out, button_2_out, not_2_out);
  D_Flip_Flop d_ff_1 (.D(in_1), .clk(and_1_out), .Q(d_ff_1_q[0]), .reset(button_1_out));  // open: Qn, preset
  D_Flip_Flop d_ff_2 (.D(d_ff_1_q[0]), .clk(and_1_out), .Q(d_ff_1_q[1]), .reset(button_1_out));  // open: Qn, preset
  D_Flip_Flop d_ff_3 (.D(d_ff_1_q[1]), .clk(and_1_out), .Q(d_ff_1_q[2]), .reset(button_1_out));  // open: Qn, preset
  D_Flip_Flop d_ff_4 (.D(d_ff_1_q[2]), .clk(and_1_out), .Q(d_ff_1_q[3]), .reset(button_1_out));  // open: Qn, preset
  or or_1 (or_1_out, button_1_out, comparator_1_eq);
  Counter #(.max('hf), .width(4)) counter_1 (
    .clr(or_1_out), .up(1'b1), .count(1'b1), .clk(and_1_out), .Q(counter_1_q));  // open: load, D, carry
  Comparator #(.mode("unsigned"), .width(4)) comparator_1 (
    .a(counter_1_q), .b(4'b0101), .eq(comparator_1_eq));  // open: gt, lt
  Comparator #(.mode("unsigned"), .width(4)) comparator_2 (
    .a(d_ff_1_q), .b(4'b1000), .eq(comparator_2_eq));  // open: gt, lt
  and and_2 (and_2_out, comparator_2_eq, comparator_3_eq);
  not not_1 (not_1_out, and_2_out);
  LED led_1 (.in(and_2_out));
  and and_3 (and_3_out, comparator_3_eq, not_1_out);
  LED led_2 (.in(and_3_out));
  Comparator #(.mode("unsigned"), .width(4)) comparator_3 (
    .a(counter_1_q), .b(4'b0100), .eq(comparator_3_eq));  // open: gt, lt
  Button button_3 (.out(button_3_out));
  or or_2 (or_2_out, button_3_out, and_2_out);
  Counter #(.max('h7), .width(3)) counter_2 (
    .clr(or_2_out), .up(1'b1), .count(1'b1), .clk(and_4_out), .Q(counter_2_q));  // open: load, D, carry
  and and_4 (and_4_out, and_3_out, comparator_3_eq);
  LED led_3 (.in(comparator_4_eq));
  Comparator #(.mode("unsigned"), .width(3)) comparator_4 (
    .a(counter_2_q), .b(3'b011), .eq(comparator_4_eq));  // open: gt, lt
  not not_2 (not_2_out, comparator_4_eq);

  // Notes on the sheet:
  //   RESET
  //   PRESS
  //   MATCHED
  //   WRONG
  //   system locked
endmodule
